# Fritzing sketch pc_switcher (saved by Fritzing 0.9.3b)
circuit board: 5.23957cm x 4.83128cm
breadboards: 1

parts:
  VCC_POWER = female pin header, 2 pins [form="♀ (female)"]
  MH-ET_LIVE_ESP32_DEVKIT1 = MH-ET LIVE ESP32 DEVKIT 38 pins
  D1 = Rectifier Diode [part_number=1N4001 package="300 mil [THT]"]
  J1_PC_SW = female pin header, 2 pins [form="♀ (female)"]
  J2_CASE_SW = female pin header, 2 pins [form="♀ (female)"]
  J3_OPTION = female pin header, 2 pins [form="♀ (female)"]
  Q1 = NPN-Transistor [package="TO92 [THT]"]

nets:
  N1: VCC_POWER.pin1, MH-ET_LIVE_ESP32_DEVKIT1.5V
  N2: VCC_POWER.pin2, MH-ET_LIVE_ESP32_DEVKIT1.GND#58
  N3: MH-ET_LIVE_ESP32_DEVKIT1.IO13, Q1.B
  N4: D1.cathode, J1_PC_SW.pin2, J3_OPTION.pin1, Q1.E
  N5: D1.anode, J2_CASE_SW.pin2, J3_OPTION.pin2
  N6: J1_PC_SW.pin1, J2_CASE_SW.pin1, Q1.C

custom parts:
  MH-ET LIVE ESP32 DEVKIT 38 pins: http://mh.nodebb.com/topic/2/mh-et-live-esp32-devkit
